// Logisim project TN1.circ as structural Verilog: 1 circuit, main circuit main
module main (
  input  A,
  input  B,
  input  C,
  output out_4,
  output out_5,
  output out_6,
  output out_7,
  output out_8,
  output out_9,
  output out_10,
  output out_11,
  output out_12,
  output out_13
);

  wire nand_3_out;

  not not_1 (out_4, A);
  and and_1 (out_5, A, B);
  or or_1 (out_6, A, B);
  nand nand_1 (out_7, A, B);
  nor nor_1 (out_8, A, B);
  xor xor_1 (out_9, A, B);
  xnor xnor_1 (out_10, A, B);
  xor xor_2 (out_11, A, B, C);
  nand nand_2 (out_12, A, B, C);
  nand nand_3 (nand_3_out, A, B);
  nand nand_4 (out_13, nand_3_out, C);
endmodule
